# Fritzing sketch EdgePowerMeter (saved by Fritzing 1.0.6)

parts:
  A1 = Esp32-c3 super mini
  S1 = 0.91 inch OLED I2C Display 128 x 32 Pixels
  A2 = ZS-042 Real Time Clock Module [part_number=DS]
  INA1 = INA219 DC Current Sensor Breakout
  C1 = Electrolytic Capacitor [capacitance=2.2mF voltage=35V package="100 mil [THT, electrolytic]"]
  A3 = USB power module
  Adafruit_Sunken_USB_Type_C_Breakout1 = Adafruit Sunken USB Type C Breakout [mn=Adafruit mpn=#6050 part_number=#6050]
  J2 = Screw terminal - 2 pins [package=THT]
  Adafruit_Sunken_USB_Type_C_Breakout2 = Adafruit Sunken USB Type C Breakout [mn=Adafruit mpn=#6050 part_number=#6050]
  J3 = Screw terminal - 2 pins [package=THT]
  Part1 = USB Type A Female Breakout Board [part_number=BOB-12700]
  C2 = Ceramic Capacitor [capacitance="100 nF" voltage=35V package="0805 [SMD, multilayer]"]

nets:
  N1: A1.Pin_4, S1.SDA, A2.SDA, INA1.SDA
  N2: A1.Pin_5, S1.SCL, A2.SCL, INA1.SCL
  N3: A1.Pin_12, A2.SQW
  GND: A1.Pin_15, S1.GND, INA1.GND
  VCC: A1.Pin_16, S1.VCC, A2.VCC, INA1.VCC
  GND_2: A2.GND, C1.-, A3.Pin_4, A3.Pin_5, A3.Pin_6, Adafruit_Sunken_USB_Type_C_Breakout1.GND, J2.pin1, Part1.GND, C2.0
  N4: INA1.Vin-2, C1.+, J3.pin1, C2.1
  N5: INA1.Vin+2, A3.Pin_3, Adafruit_Sunken_USB_Type_C_Breakout1.VBUS, J2.pin2
  N6: Adafruit_Sunken_USB_Type_C_Breakout1.CC1, Adafruit_Sunken_USB_Type_C_Breakout2.CC1
  N7: Adafruit_Sunken_USB_Type_C_Breakout1.CC2, Adafruit_Sunken_USB_Type_C_Breakout2.CC2
  N8: Adafruit_Sunken_USB_Type_C_Breakout2.GND, J3.pin2
  N9: Adafruit_Sunken_USB_Type_C_Breakout2.VBUS, Part1.VCC

notes:
  INPUT STAGE: Do not connect more than 1 port at time!
  OUTPUT STAGE: Connect here your load
  100nF ceramic
  2.2mF Electrolytic

custom parts:
  Esp32-c3 super mini: ESP32-C3 Development Board ESP32 SuperMini Development Board ESP32 Development Board WiFi Bluetooth.
  INA219 DC Current Sensor Breakout: INA DC Current Sensor Breakout
  USB power module: PD QC AFC Fast Charge Decoy Trigger Module USB-PWR Module Supports 5V 9V 12V 15V 20V Fixed Voltage Output.
  USB Type A Female Breakout Board: USB breakout board for a Type A connector. sparkfun.com
